# Fritzing sketch circuit (saved by Fritzing 0.8.7b)
breadboards: 1

parts:
  Part1 = Arduino Nano (Rev3.0)
  S1 = H-Bridge with L298N
  BAT1 = Battery Holders [package=battery-aa-kit]
  M4 = fc-51 [package=THT]
  M5 = fc-51 [package=THT]
  M6 = fc-51 [package=THT]
  M7 = fc-51 [package=THT]
  M3 = DC Motor
  M2 = DC Motor
  Part2 = HC-SR04 Ultrasonic Rangemeter
  S2 = Pushbutton [package="[THT]"]
  R1 = Resistor [package="2512 [SMD]"]

nets:
  GND: Part1.GND, S1.GND, BAT1.+, M4.pin2, M5.pin2, M6.pin2, M7.pin2, Part2.GND, S2.Pin_1, S2.Pin_2
  N1: Part1.D3, S1.IN1
  N2: Part1.D4, S1.IN2
  N3: Part1.D5, S1.IN3
  N4: Part1.D6, S1.IN4
  N5: Part1.D7, Part2.Trig
  N6: Part1.D8, Part2.Echo
  N7: Part1.D9, S2.Pin_3, S2.Pin_4, R1.Pin_1
  N8: Part1.D10, M5.pin1
  N9: Part1.D11/MOSI, M6.pin1
  N10: Part1.D12/MISO, M7.pin1
  5V: Part1.5V, S1.12V, S1.5V, BAT1.-, M4.pin3, M5.pin3, M6.pin3, M7.pin3, Part2.VCC, R1.Pin_0
  N11: Part1.A0, M4.pin1
  N12: S1.M1-01, M2.pin_2
  N13: S1.M1-02, M2.pin_1
  N14: S1.M2-01, M3.pin_2
  N15: S1.M2-02, M3.pin_1

custom parts:
  H-Bridge with L298N: h-bridge
